# Fritzing sketch rpizero_hd44780_lcd (saved by Fritzing 1.0.4)
breadboards: 1

parts:
  MCU1 = Raspberry Pi Zero
  LCD1 = LCD screen
  R1 = Resistor [tolerance=±5% power=0.25W resistance=220 package=THT]
  R2 = 12mm Trimmer Potentiometer (Large) [maximum_resistance=10kΩ knob_status=50% power=0.5W package=THT]
  D1 = Rectifier Diode [part_number=1N4001 package="Melf DO-213 AB [SMD]"]

nets:
  N1: MCU1.pin_2, LCD1.VDD, R1.Pin_1, R2.leg1, D1.cathode
  N2: MCU1.pin_6, MCU1.pin_9, MCU1.pin_30, LCD1.VSS, LCD1.R/W, LCD1.LED-, R2.leg2, D1.anode
  N3: MCU1.pin_7, LCD1.RS
  N4: MCU1.pin_11, LCD1.E
  N5: MCU1.pin_12, LCD1.DB4
  N6: MCU1.pin_15, LCD1.DB5
  N7: MCU1.pin_16, LCD1.DB6
  N8: MCU1.pin_18, LCD1.DB7
  N9: LCD1.V0, R2.wiper
  N10: LCD1.LED+, R1.Pin_0
